// Logisim project circuitomeiocorrigido.circ as structural Verilog: 9 circuits, main circuit main
module main (
  input  E1,
  input  E2,
  input  E3,
  input  E4,
  input  E1_2,
  input  E5,
  input  E2_2,
  output TF
);

  wire and_1_out, and_2_out, and_3_out, and_4_out, or_1_out, or_2_out, or_3_out, xor_1_out, xor_2_out,
       xor_3_out, xor_4_out;

  xor xor_1 (xor_1_out, E1, E2);
  and and_1 (and_1_out, E1, E2);
  or or_1 (or_1_out, xor_1_out, and_1_out);
  xor xor_2 (xor_2_out, or_1_out, E3);
  and and_2 (and_2_out, or_1_out, E3);
  xor xor_3 (xor_3_out, E4, E5);
  and and_3 (and_3_out, E4, E5);
  or or_2 (or_2_out, xor_2_out, and_2_out);
  or or_3 (or_3_out, xor_3_out, and_3_out);
  xor xor_4 (xor_4_out, or_2_out, or_3_out);
  and and_4 (and_4_out, or_3_out, or_2_out);
  xor xor_5 (TF, xor_4_out, and_4_out);

  // Notes on the sheet:
  //   T1
  //   T2
  //   T3
  //   MEIO SOMADOR
  //   T4
  //   T5
  //   T6
  //   T7
  //   T8
  //   T9
  //   T10
  //   T11
  //   S
  //   Cout
  //   COMPARADOR
  //   1 se for != e 0 se for =
  //   porta xor
endmodule

module meioSomador (
  input  E1,
  input  E2,
  input  E3,
  input  E4,
  input  E5,
  output S,
  output Cout
);

  wire and_1_out, and_2_out, and_3_out, undriven, undriven_2, undriven_3, xor_1_out, xor_2_out, xor_3_out;

  xor xor_1 (xor_1_out, E1, E2);
  and and_1 (and_1_out, E1, E2);
  xor xor_2 (xor_2_out, undriven, E3);
  and and_2 (and_2_out, undriven, E3);
  xor xor_3 (xor_3_out, E4, E5);
  and and_3 (and_3_out, E4, E5);
  xor xor_4 (S, undriven_2, undriven_3);
  and and_4 (Cout, undriven_3, undriven_2);

  // Notes on the sheet:
  //   T1
  //   T2
  //   T3
  //   T4
  //   T5
  //   T6
  //   T7
  //   T8
  //   T9
  //   T10
  //   T11
endmodule

module comparador (
  input  S,
  input  TS,
  input  in_3,
  input  in_4,
  output out_5,
  output out_6,
  output A,
  output D,
  output E,
  output F,
  output G
);

  xor xor_1 (out_5, S, TS);
  xor xor_2 (out_6, in_3, in_4);
  not not_1 (A, out_6);
  not not_2 (D, out_6);
  not not_3 (E, out_6);
  not not_4 (F, out_6);
  not not_5 (G, out_6);
  _7_Segment_Display u_7_segment_display_1 (.g(G), .f(F), .a(A), .e(E), .d(D));  // open: b, c, dp

  // Notes on the sheet:
  //   COMPARADOR
  //   porta xor
  //   a saída é 1 se os dígitos forem diferentes e 0 se os dígitos forem iguais
  //   1 0 = 2 -> tem 2 níveis alto, então, se a saída for 1 = é um código 2 de 5
  //   se for 0 mostra a mensagem de erro
  //   TF
  //   TS
  //   TF
  //   A1
  //   D1
  //   E1
  //   F1
  //   G1
  //   módulo do display 7 segmentos com os dígitos
endmodule

module decodificadorErro (
  input  COMPARADOR,
  output A,
  output D,
  output E,
  output F,
  output G
);

  not not_1 (A, COMPARADOR);
  not not_2 (D, COMPARADOR);
  not not_3 (E, COMPARADOR);
  not not_4 (F, COMPARADOR);
  not not_5 (G, COMPARADOR);
  _7_Segment_Display u_7_segment_display_1 (.g(G), .f(F), .a(A), .e(E), .d(D));  // open: b, c, dp

  // Notes on the sheet:
  //   A1
  //   D1
  //   E1
  //   F1
  //   G1
endmodule

module decodificador (
  input  E1,
  input  E2,
  input  E3,
  input  E4,
  input  E5,
  output A9,
  output B,
  output C,
  output D,
  output E,
  output F,
  output G
);

  wire and_1_out, and_2_out, and_3_out, and_4_out, and_5_out, and_6_out, and_7_out, and_8_out, and_9_out,
       and_10_out, and_11_out, and_12_out, and_13_out, and_14_out, and_15_out, and_16_out, and_17_out,
       and_18_out, and_19_out, and_20_out, and_21_out, and_22_out, and_23_out, and_24_out, and_25_out,
       and_26_out, and_27_out, and_28_out, and_29_out, and_30_out, and_31_out, and_32_out, and_33_out,
       and_34_out, and_35_out, and_36_out, and_37_out, and_38_out, and_39_out, and_40_out, and_41_out,
       and_42_out, and_43_out, and_44_out, and_45_out, and_46_out, and_47_out, and_48_out, and_49_out,
       not_1_out, not_2_out, not_3_out, not_4_out, not_5_out, not_6_out, not_7_out, not_8_out, not_9_out,
       not_10_out, not_11_out, not_12_out, not_13_out, not_14_out, not_15_out, not_16_out, not_17_out,
       not_18_out, not_19_out, not_20_out, not_21_out, not_22_out, not_23_out, not_24_out, not_25_out,
       not_26_out, not_27_out, not_28_out, not_29_out, not_30_out, not_31_out, not_32_out, not_33_out,
       not_34_out, not_35_out, not_36_out, not_37_out, not_38_out, not_39_out, not_40_out, not_41_out,
       not_42_out, not_43_out, not_44_out, not_45_out, not_46_out, not_47_out, not_48_out, not_49_out,
       not_50_out, not_51_out, not_52_out, not_53_out, not_54_out, not_55_out, not_56_out, not_57_out,
       not_58_out, not_59_out, not_60_out, not_61_out, not_62_out, not_63_out, not_64_out, not_65_out,
       not_66_out, not_67_out, not_68_out, not_69_out, not_70_out, not_71_out, not_72_out, not_73_out,
       not_74_out, not_75_out, not_76_out, not_77_out, not_78_out, not_79_out, not_80_out, not_81_out,
       not_82_out, not_83_out, not_84_out, not_85_out, not_86_out, not_87_out, not_88_out, not_89_out,
       not_90_out, not_91_out, not_92_out, not_93_out, not_94_out, not_95_out, not_96_out, not_97_out,
       not_98_out, not_99_out, not_100_out, not_101_out, not_102_out, not_103_out, not_104_out, not_105_out,
       not_106_out, not_107_out, not_108_out, not_109_out, not_110_out, not_111_out, not_112_out,
       not_113_out, not_114_out, not_115_out, not_116_out, not_117_out, not_118_out, not_119_out,
       not_120_out, not_121_out, not_122_out, not_123_out, not_124_out, not_125_out, not_126_out,
       not_127_out, not_128_out, not_129_out, not_130_out, not_131_out, not_132_out, not_133_out,
       not_134_out, not_135_out, not_136_out, not_137_out, not_138_out, not_139_out, not_140_out,
       not_141_out, not_142_out, not_143_out, not_144_out, not_145_out, not_146_out, not_147_out;

  not not_1 (not_1_out, E3);
  not not_2 (not_2_out, E4);
  not not_3 (not_3_out, E5);
  not not_4 (not_4_out, E1);
  not not_5 (not_5_out, E3);
  not not_6 (not_6_out, E4);
  not not_7 (not_7_out, E2);
  not not_8 (not_8_out, E3);
  not not_9 (not_9_out, E4);
  not not_10 (not_10_out, E1);
  not not_11 (not_11_out, E2);
  not not_12 (not_12_out, E3);
  not not_13 (not_13_out, E2);
  not not_14 (not_14_out, E3);
  not not_15 (not_15_out, E5);
  not not_16 (not_16_out, E1);
  not not_17 (not_17_out, E2);
  not not_18 (not_18_out, E5);
  not not_19 (not_19_out, E1);
  not not_20 (not_20_out, E4);
  not not_21 (not_21_out, E5);
  not not_22 (not_22_out, E2);
  not not_23 (not_23_out, E4);
  not not_24 (not_24_out, E5);
  not not_25 (not_25_out, E3);
  not not_26 (not_26_out, E4);
  not not_27 (not_27_out, E5);
  not not_28 (not_28_out, E1);
  not not_29 (not_29_out, E3);
  not not_30 (not_30_out, E4);
  not not_31 (not_31_out, E1);
  not not_32 (not_32_out, E2);
  not not_33 (not_33_out, E3);
  not not_34 (not_34_out, E1);
  not not_35 (not_35_out, E3);
  not not_36 (not_36_out, E5);
  not not_37 (not_37_out, E2);
  not not_38 (not_38_out, E3);
  not not_39 (not_39_out, E5);
  not not_40 (not_40_out, E1);
  not not_41 (not_41_out, E2);
  not not_42 (not_42_out, E5);
  not not_43 (not_43_out, E1);
  not not_44 (not_44_out, E2);
  not not_45 (not_45_out, E4);
  not not_46 (not_46_out, E2);
  not not_47 (not_47_out, E4);
  not not_48 (not_48_out, E5);
  not not_49 (not_49_out, E3);
  not not_50 (not_50_out, E4);
  not not_51 (not_51_out, E5);
  not not_52 (not_52_out, E1);
  not not_53 (not_53_out, E3);
  not not_54 (not_54_out, E4);
  not not_55 (not_55_out, E2);
  not not_56 (not_56_out, E3);
  not not_57 (not_57_out, E4);
  not not_58 (not_58_out, E1);
  not not_59 (not_59_out, E2);
  not not_60 (not_60_out, E3);
  not not_61 (not_61_out, E1);
  not not_62 (not_62_out, E3);
  not not_63 (not_63_out, E5);
  not not_64 (not_64_out, E2);
  not not_65 (not_65_out, E3);
  not not_66 (not_66_out, E5);
  not not_67 (not_67_out, E1);
  not not_68 (not_68_out, E2);
  not not_69 (not_69_out, E4);
  not not_70 (not_70_out, E1);
  not not_71 (not_71_out, E4);
  not not_72 (not_72_out, E5);
  not not_73 (not_73_out, E2);
  not not_74 (not_74_out, E4);
  not not_75 (not_75_out, E5);
  not not_76 (not_76_out, E3);
  not not_77 (not_77_out, E4);
  not not_78 (not_78_out, E5);
  not not_79 (not_79_out, E1);
  not not_80 (not_80_out, E3);
  not not_81 (not_81_out, E4);
  not not_82 (not_82_out, E2);
  not not_83 (not_83_out, E3);
  not not_84 (not_84_out, E4);
  not not_85 (not_85_out, E1);
  not not_86 (not_86_out, E2);
  not not_87 (not_87_out, E3);
  not not_88 (not_88_out, E1);
  not not_89 (not_89_out, E2);
  not not_90 (not_90_out, E5);
  not not_91 (not_91_out, E1);
  not not_92 (not_92_out, E4);
  not not_93 (not_93_out, E5);
  not not_94 (not_94_out, E2);
  not not_95 (not_95_out, E4);
  not not_96 (not_96_out, E5);
  not not_97 (not_97_out, E2);
  not not_98 (not_98_out, E3);
  not not_99 (not_99_out, E4);
  not not_100 (not_100_out, E1);
  not not_101 (not_101_out, E2);
  not not_102 (not_102_out, E3);
  not not_103 (not_103_out, E1);
  not not_104 (not_104_out, E2);
  not not_105 (not_105_out, E5);
  not not_106 (not_106_out, E2);
  not not_107 (not_107_out, E4);
  not not_108 (not_108_out, E5);
  not not_109 (not_109_out, E3);
  not not_110 (not_110_out, E4);
  not not_111 (not_111_out, E5);
  not not_112 (not_112_out, E2);
  not not_113 (not_113_out, E3);
  not not_114 (not_114_out, E4);
  not not_115 (not_115_out, E1);
  not not_116 (not_116_out, E2);
  not not_117 (not_117_out, E3);
  not not_118 (not_118_out, E1);
  not not_119 (not_119_out, E3);
  not not_120 (not_120_out, E5);
  not not_121 (not_121_out, E1);
  not not_122 (not_122_out, E4);
  not not_123 (not_123_out, E5);
  not not_124 (not_124_out, E2);
  not not_125 (not_125_out, E4);
  not not_126 (not_126_out, E5);
  not not_127 (not_127_out, E3);
  not not_128 (not_128_out, E4);
  not not_129 (not_129_out, E5);
  not not_130 (not_130_out, E1);
  not not_131 (not_131_out, E3);
  not not_132 (not_132_out, E4);
  not not_133 (not_133_out, E2);
  not not_134 (not_134_out, E3);
  not not_135 (not_135_out, E4);
  not not_136 (not_136_out, E1);
  not not_137 (not_137_out, E3);
  not not_138 (not_138_out, E5);
  not not_139 (not_139_out, E1);
  not not_140 (not_140_out, E2);
  not not_141 (not_141_out, E5);
  not not_142 (not_142_out, E1);
  not not_143 (not_143_out, E4);
  not not_144 (not_144_out, E5);
  not not_145 (not_145_out, E2);
  not not_146 (not_146_out, E4);
  not not_147 (not_147_out, E5);
  and and_1 (and_1_out, E1, E2, not_1_out, not_2_out, not_3_out);
  and and_2 (and_2_out, not_4_out, E2, not_5_out, not_6_out, E5);
  and and_3 (and_3_out, E1, not_7_out, not_8_out, not_9_out, E5);
  and and_4 (and_4_out, not_10_out, not_11_out, not_12_out, E4, E5);
  and and_5 (and_5_out, E1, not_13_out, not_14_out, E4, not_15_out);
  and and_6 (and_6_out, not_16_out, not_17_out, E3, E4, not_18_out);
  and and_7 (and_7_out, not_19_out, E2, E3, not_20_out, not_21_out);
  and and_8 (and_8_out, E1, not_22_out, E3, not_23_out, not_24_out);
  and and_9 (and_9_out, E1, E2, not_25_out, not_26_out, not_27_out);
  and and_10 (and_10_out, not_28_out, E2, not_29_out, not_30_out, E5);
  and and_11 (and_11_out, not_31_out, not_32_out, not_33_out, E4, E5);
  and and_12 (and_12_out, not_34_out, E2, not_35_out, E4, not_36_out);
  and and_13 (and_13_out, E1, not_37_out, not_38_out, E4, not_39_out);
  and and_14 (and_14_out, not_40_out, not_41_out, E3, E4, not_42_out);
  and and_15 (and_15_out, not_43_out, not_44_out, E3, not_45_out, E5);
  and and_16 (and_16_out, E1, not_46_out, E3, not_47_out, not_48_out);
  and and_17 (and_17_out, E1, E2, not_49_out, not_50_out, not_51_out);
  and and_18 (and_18_out, not_52_out, E2, not_53_out, not_54_out, E5);
  and and_19 (and_19_out, E1, not_55_out, not_56_out, not_57_out, E5);
  and and_20 (and_20_out, not_58_out, not_59_out, not_60_out, E4, E5);
  and and_21 (and_21_out, not_61_out, E2, not_62_out, E4, not_63_out);
  and and_22 (and_22_out, E1, not_64_out, not_65_out, E4, not_66_out);
  and and_23 (and_23_out, not_67_out, not_68_out, E3, not_69_out, E5);
  and and_24 (and_24_out, not_70_out, E2, E3, not_71_out, not_72_out);
  and and_25 (and_25_out, E1, not_73_out, E3, not_74_out, not_75_out);
  and and_26 (and_26_out, E1, E2, not_76_out, not_77_out, not_78_out);
  and and_27 (and_27_out, not_79_out, E2, not_80_out, not_81_out, E5);
  and and_28 (and_28_out, E1, not_82_out, not_83_out, not_84_out, E5);
  and and_29 (and_29_out, not_85_out, not_86_out, not_87_out, E4);
  and and_30 (and_30_out, not_88_out, not_89_out, E4, not_90_out);
  and and_31 (and_31_out, not_91_out, E2, E3, not_92_out, not_93_out);
  and and_32 (and_32_out, E1, not_94_out, E3, not_95_out, not_96_out);
  and and_33 (and_33_out, E1, not_97_out, not_98_out, not_99_out, E5);
  and and_34 (and_34_out, not_100_out, not_101_out, not_102_out, E4, E5);
  and and_35 (and_35_out, not_103_out, not_104_out, E3, E4, not_105_out);
  and and_36 (and_36_out, E1, not_106_out, E3, not_107_out, not_108_out);
  and and_37 (and_37_out, E1, E2, not_109_out, not_110_out, not_111_out);
  and and_38 (and_38_out, E1, not_112_out, not_113_out, not_114_out, E5);
  and and_39 (and_39_out, not_115_out, not_116_out, not_117_out, E4, E5);
  and and_40 (and_40_out, not_118_out, E2, not_119_out, E4, not_120_out);
  and and_41 (and_41_out, not_121_out, E2, E3, not_122_out, not_123_out);
  and and_42 (and_42_out, E1, not_124_out, E3, not_125_out, not_126_out);
  and and_43 (and_43_out, E1, E2, not_127_out, not_128_out, not_129_out);
  and and_44 (and_44_out, not_130_out, E2, not_131_out, not_132_out, E5);
  and and_45 (and_45_out, E1, not_133_out, not_134_out, not_135_out, E5);
  and and_46 (and_46_out, not_136_out, E2, not_137_out, E4, not_138_out);
  and and_47 (and_47_out, not_139_out, not_140_out, E3, E4, not_141_out);
  and and_48 (and_48_out, not_142_out, E2, E3, not_143_out, not_144_out);
  and and_49 (and_49_out, E1, not_145_out, E3, not_146_out, not_147_out);
  or or_1 (A9, and_1_out, and_2_out, and_3_out, and_4_out, and_5_out, and_6_out, and_7_out, and_8_out);
  or or_2 (B, and_9_out, and_10_out, and_11_out, and_12_out, and_13_out, and_14_out, and_15_out, and_16_out);
  or or_3 (C, and_17_out, and_18_out, and_19_out, and_20_out, and_21_out, and_22_out, and_23_out, and_24_out, and_25_out);
  or or_4 (D, and_26_out, and_27_out, and_28_out, and_29_out, and_30_out, and_31_out, and_32_out);
  or or_5 (E, and_33_out, and_34_out, and_35_out, and_36_out);
  or or_6 (F, and_37_out, and_38_out, and_39_out, and_40_out, and_41_out, and_42_out);
  or or_7 (G, and_43_out, and_44_out, and_45_out, and_46_out, and_47_out, and_48_out, and_49_out);
  _7_Segment_Display u_7_segment_display_1 (.g(G), .f(F), .a(A9), .b(B), .e(E), .d(D), .c(C));  // open: dp

  // Notes on the sheet:
  //   SEGMENTO B
  //   SEGMENTO C
  //   SEGMENTO D
  //   SEGMENTO E
  //   SEGMENTO F
  //   SEGMENTO G
  //   SEGMENTO A
  //   A4
  //   A5
  //   B1
  //   B2
  //   B3
  //   B4
  //   B5
  //   B8
  //   A1
  //   A2
  //   A3
  //   A6
  //   A7
  //   A8
  //   B6
  //   B7
  //   C1
  //   C2
  //   C3
  //   C4
  //   C5
  //   C6
  //   C7
  //   C8
  //   C9
  //   D1
  //   D2
  //   D3
  //   D4
  //   D5
  //   D6
  //   D7
  //   Ee1
  //   Ee2
  //   Ee3
  //   Ee4
  //   F1
  //   F2
  //   F3
  //   F4
  //   F5
  //   F6
  //   G1
  //   G2
  //   G3
  //   G4
  //   G5
  //   G6
  //   G7
  //   B9
  //   C10
  //   SB
  //   SD
  //   D8
  //   SE
  //   Ee5
  //   F7
  //   G8
  //   SF
  //   GS
  //   SA
endmodule

module matriz (
  input  A,
  input  B,
  input  C
);

  wire not_1_out, not_2_out, not_3_out, not_4_out, not_5_out, not_6_out, not_7_out, not_8_out, not_9_out,
       not_10_out, not_11_out, not_12_out, not_13_out;

  not not_1 (not_1_out, C);
  not not_2 (not_2_out, B);
  not not_3 (not_3_out, B);
  not not_4 (not_4_out, C);
  not not_5 (not_5_out, A);
  not not_6 (not_6_out, C);
  not not_7 (not_7_out, A);
  not not_8 (not_8_out, C);
  not not_9 (not_9_out, A);
  not not_10 (not_10_out, B);
  not not_11 (not_11_out, A);
  not not_12 (not_12_out, B);
  not not_13 (not_13_out, C);
  // AND_Gate and_1 has open pins: in0=A, in1=B, in2=not_1_out, out=open
  // AND_Gate and_2 has open pins: in0=A, in1=not_2_out, in2=C, out=open
  // AND_Gate and_3 has open pins: in0=A, in1=not_3_out, in2=not_4_out, out=open
  // AND_Gate and_4 has open pins: in0=not_5_out, in1=B, in2=not_6_out, out=open
  // AND_Gate and_5 has open pins: in0=not_7_out, in1=B, in2=not_8_out, out=open
  // AND_Gate and_6 has open pins: in0=not_9_out, in1=not_10_out, in2=C, out=open
  // AND_Gate and_7 has open pins: in0=not_11_out, in1=not_12_out, in2=not_13_out, out=open

  // Notes on the sheet:
  //   L1 = A.B.C' 			
  //   L2 = A.B'.C
  //   L3 = A.B'.C'
  //   L4 = A'.B.C'
  //   L5 = A'. B.C'
  //   L6 = A'.B'.C
  //   L7 = A'.B'.C'
endmodule

module teste (
  input  E1,
  input  E2,
  input  E3,
  input  E4,
  input  E5,
  input  A,
  input  in_7,
  input  in_8,
  input  Fc1,
  input  in_10,
  input  COLUNAS,
  input  in_12,
  input  in_13,
  output out_14,
  output out_15,
  output out_16,
  output out_17,
  output out_18,
  output out_19,
  output out_20,
  output out_21,
  output out_22,
  output B,
  output out_24,
  output C,
  output D,
  output E,
  output F,
  output A_2,
  output D_2,
  output E_2,
  output G,
  output F_2,
  output G_2
);

  wire and_8_out, and_9_out, and_10_out, and_11_out, and_12_out, and_13_out, and_14_out, and_15_out,
       and_16_out, and_17_out, and_18_out, and_19_out, and_20_out, and_21_out, and_22_out, and_23_out,
       and_24_out, and_25_out, and_26_out, and_27_out, and_28_out, and_29_out, and_30_out, and_31_out,
       and_32_out, and_33_out, and_34_out, and_35_out, and_36_out, and_37_out, and_38_out, and_39_out,
       and_40_out, and_41_out, and_42_out, and_43_out, and_44_out, and_45_out, and_46_out, and_47_out,
       and_48_out, and_49_out, and_50_out, and_51_out, and_52_out, and_53_out, and_54_out, and_55_out,
       and_56_out, and_57_out, and_58_out, and_59_out, and_60_out, not_1_out, not_2_out, not_3_out,
       not_4_out, not_5_out, not_6_out, not_7_out, not_8_out, not_9_out, not_10_out, not_11_out, not_12_out,
       not_13_out, not_14_out, not_15_out, not_16_out, not_17_out, not_18_out, not_19_out, not_20_out,
       not_21_out, not_22_out, not_23_out, not_24_out, not_25_out, not_26_out, not_27_out, not_28_out,
       not_29_out, not_30_out, not_31_out, not_32_out, not_33_out, not_34_out, not_35_out, not_36_out,
       not_37_out, not_38_out, not_39_out, not_40_out, not_41_out, not_42_out, not_43_out, not_44_out,
       not_45_out, not_46_out, not_47_out, not_48_out, not_49_out, not_50_out, not_51_out, not_52_out,
       not_53_out, not_54_out, not_55_out, not_56_out, not_57_out, not_58_out, not_59_out, not_60_out,
       not_61_out, not_62_out, not_63_out, not_64_out, not_65_out, not_66_out, not_67_out, not_68_out,
       not_69_out, not_70_out, not_71_out, not_72_out, not_73_out, not_74_out, not_75_out, not_76_out,
       not_77_out, not_78_out, not_79_out, not_80_out, not_81_out, not_82_out, not_83_out, not_84_out,
       not_85_out, not_86_out, not_87_out, not_88_out, not_89_out, not_90_out, not_91_out, not_92_out,
       not_93_out, not_94_out, not_95_out, not_96_out, not_97_out, not_98_out, not_99_out, not_100_out,
       not_101_out, not_102_out, not_103_out, not_104_out, not_105_out, not_106_out, not_107_out,
       not_108_out, not_109_out, not_110_out, not_111_out, not_112_out, not_113_out, not_114_out,
       not_115_out, not_116_out, not_117_out, not_118_out, not_119_out, not_120_out, not_121_out,
       not_122_out, not_123_out, not_124_out, not_125_out, not_126_out, not_127_out, not_128_out,
       not_129_out, not_130_out, not_131_out, not_132_out, not_133_out, not_134_out, not_135_out,
       not_136_out, not_137_out, not_138_out, not_139_out, not_140_out, not_141_out, not_142_out,
       not_143_out, not_144_out, not_145_out, not_146_out, not_147_out, not_148_out, not_149_out,
       not_150_out, not_151_out, not_152_out, not_153_out, not_154_out, not_155_out, not_156_out,
       not_157_out, not_158_out, not_159_out, not_160_out, not_161_out, not_162_out, not_163_out,
       not_164_out, not_165_out, not_166_out, not_167_out, not_168_out, not_169_out, not_170_out,
       not_171_out, not_172_out, not_173_out, or_10_out, or_11_out;

  or or_1 (out_14, A, in_7, in_8);
  not not_1 (not_1_out, out_14);
  not not_2 (not_2_out, COLUNAS);
  not not_3 (not_3_out, in_12);
  not not_4 (not_4_out, in_13);
  not not_5 (not_5_out, in_10);
  not not_6 (not_6_out, COLUNAS);
  not not_7 (not_7_out, in_12);
  not not_8 (not_8_out, in_10);
  not not_9 (not_9_out, COLUNAS);
  not not_10 (not_10_out, in_13);
  not not_11 (not_11_out, in_10);
  not not_12 (not_12_out, in_12);
  not not_13 (not_13_out, in_13);
  not not_14 (not_14_out, in_8);
  not not_15 (not_15_out, in_7);
  not not_16 (not_16_out, in_7);
  not not_17 (not_17_out, in_8);
  not not_18 (not_18_out, A);
  not not_19 (not_19_out, in_8);
  not not_20 (not_20_out, A);
  not not_21 (not_21_out, in_8);
  not not_22 (not_22_out, A);
  not not_23 (not_23_out, in_7);
  not not_24 (not_24_out, A);
  not not_25 (not_25_out, in_7);
  not not_26 (not_26_out, in_8);
  and and_1 (out_16, A, in_7, not_14_out);
  and and_2 (out_17, A, not_15_out, in_8);
  and and_3 (out_18, A, not_16_out, not_17_out);
  and and_4 (out_19, not_18_out, in_7, not_19_out);
  and and_5 (out_20, not_20_out, in_7, not_21_out);
  and and_6 (out_21, not_22_out, not_23_out, in_8);
  and and_7 (out_22, not_24_out, not_25_out, not_26_out);
  and and_8 (and_8_out, out_14, Fc1, in_10, not_2_out, not_3_out, not_4_out);
  and and_9 (and_9_out, out_14, Fc1, not_5_out, not_6_out, not_7_out, in_13);
  and and_10 (and_10_out, out_14, Fc1, not_8_out, not_9_out, in_12, not_10_out);
  and and_11 (and_11_out, out_14, Fc1, not_11_out, COLUNAS, not_12_out, not_13_out);
  or or_2 (out_24, and_8_out, and_9_out, and_10_out, and_11_out);
  not not_27 (not_27_out, E3);
  not not_28 (not_28_out, E4);
  not not_29 (not_29_out, E5);
  not not_30 (not_30_out, E1);
  not not_31 (not_31_out, E3);
  not not_32 (not_32_out, E4);
  not not_33 (not_33_out, E2);
  not not_34 (not_34_out, E3);
  not not_35 (not_35_out, E4);
  not not_36 (not_36_out, E1);
  not not_37 (not_37_out, E2);
  not not_38 (not_38_out, E3);
  not not_39 (not_39_out, E2);
  not not_40 (not_40_out, E3);
  not not_41 (not_41_out, E5);
  not not_42 (not_42_out, E1);
  not not_43 (not_43_out, E2);
  not not_44 (not_44_out, E5);
  not not_45 (not_45_out, E1);
  not not_46 (not_46_out, E4);
  not not_47 (not_47_out, E5);
  not not_48 (not_48_out, E2);
  not not_49 (not_49_out, E4);
  not not_50 (not_50_out, E5);
  not not_51 (not_51_out, E3);
  not not_52 (not_52_out, E4);
  not not_53 (not_53_out, E5);
  not not_54 (not_54_out, E1);
  not not_55 (not_55_out, E3);
  not not_56 (not_56_out, E4);
  not not_57 (not_57_out, E1);
  not not_58 (not_58_out, E2);
  not not_59 (not_59_out, E3);
  not not_60 (not_60_out, E1);
  not not_61 (not_61_out, E3);
  not not_62 (not_62_out, E5);
  not not_63 (not_63_out, E2);
  not not_64 (not_64_out, E3);
  not not_65 (not_65_out, E5);
  not not_66 (not_66_out, E1);
  not not_67 (not_67_out, E2);
  not not_68 (not_68_out, E5);
  not not_69 (not_69_out, E1);
  not not_70 (not_70_out, E2);
  not not_71 (not_71_out, E4);
  not not_72 (not_72_out, E2);
  not not_73 (not_73_out, E4);
  not not_74 (not_74_out, E5);
  not not_75 (not_75_out, E3);
  not not_76 (not_76_out, E4);
  not not_77 (not_77_out, E5);
  not not_78 (not_78_out, E1);
  not not_79 (not_79_out, E3);
  not not_80 (not_80_out, E4);
  not not_81 (not_81_out, E2);
  not not_82 (not_82_out, E3);
  not not_83 (not_83_out, E4);
  not not_84 (not_84_out, E1);
  not not_85 (not_85_out, E2);
  not not_86 (not_86_out, E3);
  not not_87 (not_87_out, E1);
  not not_88 (not_88_out, E3);
  not not_89 (not_89_out, E5);
  not not_90 (not_90_out, E2);
  not not_91 (not_91_out, E3);
  not not_92 (not_92_out, E5);
  not not_93 (not_93_out, E1);
  not not_94 (not_94_out, E2);
  not not_95 (not_95_out, E4);
  not not_96 (not_96_out, E1);
  not not_97 (not_97_out, E4);
  not not_98 (not_98_out, E5);
  not not_99 (not_99_out, E2);
  not not_100 (not_100_out, E4);
  not not_101 (not_101_out, E5);
  not not_102 (not_102_out, E3);
  not not_103 (not_103_out, E4);
  not not_104 (not_104_out, E5);
  not not_105 (not_105_out, E1);
  not not_106 (not_106_out, E3);
  not not_107 (not_107_out, E4);
  not not_108 (not_108_out, E2);
  not not_109 (not_109_out, E3);
  not not_110 (not_110_out, E4);
  not not_111 (not_111_out, E1);
  not not_112 (not_112_out, E2);
  not not_113 (not_113_out, E3);
  not not_114 (not_114_out, E1);
  not not_115 (not_115_out, E2);
  not not_116 (not_116_out, E5);
  not not_117 (not_117_out, E1);
  not not_118 (not_118_out, E4);
  not not_119 (not_119_out, E5);
  not not_120 (not_120_out, E2);
  not not_121 (not_121_out, E4);
  not not_122 (not_122_out, E5);
  not not_123 (not_123_out, E2);
  not not_124 (not_124_out, E3);
  not not_125 (not_125_out, E4);
  not not_126 (not_126_out, E1);
  not not_127 (not_127_out, E2);
  not not_128 (not_128_out, E3);
  not not_129 (not_129_out, E1);
  not not_130 (not_130_out, E2);
  not not_131 (not_131_out, E5);
  not not_132 (not_132_out, E2);
  not not_133 (not_133_out, E4);
  not not_134 (not_134_out, E5);
  not not_135 (not_135_out, E3);
  not not_136 (not_136_out, E4);
  not not_137 (not_137_out, E5);
  not not_138 (not_138_out, E2);
  not not_139 (not_139_out, E3);
  not not_140 (not_140_out, E4);
  not not_141 (not_141_out, E1);
  not not_142 (not_142_out, E2);
  not not_143 (not_143_out, E3);
  not not_144 (not_144_out, E1);
  not not_145 (not_145_out, E3);
  not not_146 (not_146_out, E5);
  not not_147 (not_147_out, E1);
  not not_148 (not_148_out, E4);
  not not_149 (not_149_out, E5);
  not not_150 (not_150_out, E2);
  not not_151 (not_151_out, E4);
  not not_152 (not_152_out, E5);
  not not_153 (not_153_out, E3);
  not not_154 (not_154_out, E4);
  not not_155 (not_155_out, E5);
  not not_156 (not_156_out, E1);
  not not_157 (not_157_out, E3);
  not not_158 (not_158_out, E4);
  not not_159 (not_159_out, E2);
  not not_160 (not_160_out, E3);
  not not_161 (not_161_out, E4);
  not not_162 (not_162_out, E1);
  not not_163 (not_163_out, E3);
  not not_164 (not_164_out, E5);
  not not_165 (not_165_out, E1);
  not not_166 (not_166_out, E2);
  not not_167 (not_167_out, E5);
  not not_168 (not_168_out, E1);
  not not_169 (not_169_out, E4);
  not not_170 (not_170_out, E5);
  not not_171 (not_171_out, E2);
  not not_172 (not_172_out, E4);
  not not_173 (not_173_out, E5);
  and and_12 (and_12_out, not_1_out, E1, E2, not_27_out, not_28_out, not_29_out);
  and and_13 (and_13_out, not_1_out, not_30_out, E2, not_31_out, not_32_out, E5);
  and and_14 (and_14_out, not_1_out, E1, not_33_out, not_34_out, not_35_out, E5);
  and and_15 (and_15_out, not_1_out, not_36_out, not_37_out, not_38_out, E4, E5);
  and and_16 (and_16_out, not_1_out, E1, not_39_out, not_40_out, E4, not_41_out);
  and and_17 (and_17_out, not_1_out, not_42_out, not_43_out, E3, E4, not_44_out);
  and and_18 (and_18_out, not_1_out, not_45_out, E2, E3, not_46_out, not_47_out);
  and and_19 (and_19_out, not_1_out, E1, not_48_out, E3, not_49_out, not_50_out);
  and and_20 (and_20_out, not_1_out, E1, E2, not_51_out, not_52_out, not_53_out);
  and and_21 (and_21_out, not_1_out, not_54_out, E2, not_55_out, not_56_out, E5);
  and and_22 (and_22_out, not_1_out, not_57_out, not_58_out, not_59_out, E4, E5);
  and and_23 (and_23_out, not_1_out, not_60_out, E2, not_61_out, E4, not_62_out);
  and and_24 (and_24_out, not_1_out, E1, not_63_out, not_64_out, E4, not_65_out);
  and and_25 (and_25_out, not_1_out, not_66_out, not_67_out, E3, E4, not_68_out);
  and and_26 (and_26_out, not_1_out, not_69_out, not_70_out, E3, not_71_out, E5);
  and and_27 (and_27_out, not_1_out, E1, not_72_out, E3, not_73_out, not_74_out);
  and and_28 (and_28_out, E1, E2, not_75_out, not_76_out, not_77_out);
  and and_29 (and_29_out, not_1_out, not_78_out, E2, not_79_out, not_80_out, E5);
  and and_30 (and_30_out, not_1_out, E1, not_81_out, not_82_out, not_83_out, E5);
  and and_31 (and_31_out, not_1_out, not_84_out, not_85_out, not_86_out, E4, E5);
  and and_32 (and_32_out, not_1_out, not_87_out, E2, not_88_out, E4, not_89_out);
  and and_33 (and_33_out, not_1_out, E1, not_90_out, not_91_out, E4, not_92_out);
  and and_34 (and_34_out, not_1_out, not_93_out, not_94_out, E3, not_95_out, E5);
  and and_35 (and_35_out, not_1_out, not_96_out, E2, E3, not_97_out, not_98_out);
  and and_36 (and_36_out, not_1_out, E1, not_99_out, E3, not_100_out, not_101_out);
  and and_37 (and_37_out, not_1_out, E1, E2, not_102_out, not_103_out, not_104_out);
  and and_38 (and_38_out, not_1_out, not_105_out, E2, not_106_out, not_107_out, E5);
  and and_39 (and_39_out, not_1_out, E1, not_108_out, not_109_out, not_110_out, E5);
  and and_40 (and_40_out, not_1_out, not_111_out, not_112_out, not_113_out, E4);
  and and_41 (and_41_out, not_1_out, not_114_out, not_115_out, E4, not_116_out);
  and and_42 (and_42_out, not_1_out, not_117_out, E2, E3, not_118_out, not_119_out);
  and and_43 (and_43_out, not_1_out, E1, not_120_out, E3, not_121_out, not_122_out);
  and and_44 (and_44_out, not_1_out, E1, not_123_out, not_124_out, not_125_out, E5);
  and and_45 (and_45_out, not_1_out, not_126_out, not_127_out, not_128_out, E4, E5);
  and and_46 (and_46_out, not_1_out, not_129_out, not_130_out, E3, E4, not_131_out);
  and and_47 (and_47_out, not_1_out, E1, not_132_out, E3, not_133_out, not_134_out);
  and and_48 (and_48_out, not_1_out, E1, E2, not_135_out, not_136_out, not_137_out);
  and and_49 (and_49_out, not_1_out, E1, not_138_out, not_139_out, not_140_out, E5);
  and and_50 (and_50_out, not_1_out, not_141_out, not_142_out, not_143_out, E4, E5);
  and and_51 (and_51_out, not_1_out, not_144_out, E2, not_145_out, E4, not_146_out);
  and and_52 (and_52_out, not_1_out, not_147_out, E2, E3, not_148_out, not_149_out);
  and and_53 (and_53_out, not_1_out, E1, not_150_out, E3, not_151_out, not_152_out);
  and and_54 (and_54_out, not_1_out, E1, E2, not_153_out, not_154_out, not_155_out);
  and and_55 (and_55_out, not_1_out, not_156_out, E2, not_157_out, not_158_out, E5);
  and and_56 (and_56_out, not_1_out, E1, not_159_out, not_160_out, not_161_out, E5);
  and and_57 (and_57_out, not_1_out, not_162_out, E2, not_163_out, E4, not_164_out);
  and and_58 (and_58_out, not_1_out, not_165_out, not_166_out, E3, E4, not_167_out);
  and and_59 (and_59_out, not_1_out, not_168_out, E2, E3, not_169_out, not_170_out);
  and and_60 (and_60_out, not_1_out, E1, not_171_out, E3, not_172_out, not_173_out);
  or or_3 (out_15, and_12_out, and_13_out, and_14_out, and_15_out, and_16_out, and_17_out, and_18_out, and_19_out);
  or or_4 (B, and_20_out, and_21_out, and_22_out, and_23_out, and_24_out, and_25_out, and_26_out, and_27_out);
  or or_5 (C, and_28_out, and_29_out, and_30_out, and_31_out, and_32_out, and_33_out, and_34_out, and_35_out, and_36_out);
  or or_6 (D, and_37_out, and_38_out, and_39_out, and_40_out, and_41_out, and_42_out, and_43_out);
  or or_7 (E, and_44_out, and_45_out, and_46_out, and_47_out);
  or or_8 (F, and_48_out, and_49_out, and_50_out, and_51_out, and_52_out, and_53_out);
  or or_9 (G, and_54_out, and_55_out, and_56_out, and_57_out, and_58_out, and_59_out, and_60_out);
  _7_Segment_Display u_7_segment_display_1 (.g(G), .f(F), .a(out_15), .b(B), .e(E), .d(D), .c(C));  // open: dp
  not not_174 (A_2, or_11_out);
  not not_175 (D_2, or_11_out);
  not not_176 (E_2, or_11_out);
  not not_177 (F_2, or_11_out);
  not not_178 (G_2, or_11_out);
  or or_10 (or_10_out, out_15, B, C, D, E, F, G);
  or or_11 (or_11_out, out_14, or_10_out);
  _7_Segment_Display u_7_segment_display_2 (.g(G_2), .f(F_2), .a(A_2), .e(E_2), .d(D_2));  // open: b, c, dp

  // Notes on the sheet:
  //   B
  //   C
  //   S3
  //   Fc2
  //   Fc3
  //   Fc4
  //   ==LINHAS==
  //   L1 = A.B.C' 			
  //   L2 = A.B'.C
  //   L3 = A.B'.C'
  //   L4 = A'.B.C'
  //   L5 = A'. B.C'
  //   L6 = A'.B'.C
  //   L7 = A'.B'.C'
  //   C1A
  //   C1B
  //   C1C
  //   C1D
  //   notA1
  //   notA2
  //   notB1
  //   SEGMENTO C
  //   SEGMENTO A
  //   SEGMENTO B
  //   SEGMENTO D
  //   SEGMENTO F
  //   SEGMENTO G
  //   A1
  //   A2
  //   A3
  //   A4
  //   A5
  //   A6
  //   A7
  //   A8
  //   B1
  //   B2
  //   B3
  //   B4
  //   B5
  //   B6
  //   B7
  //   B8
  //   C1
  //   C2
  //   C3
  //   C4
  //   C5
  //   C6
  //   C7
  //   C8
  //   C9
  //   D1
  //   D2
  //   D3
  //   D4
  //   D5
  //   D6
  //   D7
  //   SEGMENTO E
  //   Ee1
  //   Ee2
  //   Ee3
  //   Ee4
  //   F1
  //   F2
  //   F3
  //   F4
  //   F5
  //   F6
  //   G1
  //   G2
  //   G3
  //   G4
  //   G5
  //   G6
  //   G7
  //   A9
  //   B9
  //   C10
  //   D8
  //   Ee5
  //   F7
  //   G8
  //   SB
  //   SD
  //   SE
  //   SF
  //   GS
  //   SA
  //   A1
  //   D1
  //   E1
  //   F1
  //   G1
  //   or Or0(somaD, A9, B9, C10, D8, Ee5, F7, G8)
  //   somaD
  //   Erro
  //   s3
  //   or Or1(Erro, S3, somaD);
endmodule

module somadorCorrigido (
  input  E1,
  input  E2,
  input  E1_2,
  input  E2_2
);

  wire and_1_out, and_2_out, xor_1_out, xor_2_out;

  xor xor_1 (xor_1_out, E1_2, E2_2);
  and and_1 (and_1_out, E1_2, E2_2);
  xor xor_2 (xor_2_out, E1, E2);
  and and_2 (and_2_out, E1, E2);

  // Notes on the sheet:
  //   T1
  //   T2
  //   T1
  //   T2
endmodule

module testeerrodisp (
  input  E1,
  input  E2,
  input  E3,
  input  E4,
  input  E5,
  output A9,
  output B,
  output C,
  output D,
  output E,
  output F,
  output G,
  output A,
  output D_2,
  output E_2,
  output F_2,
  output G_2
);

  wire and_1_out, and_2_out, and_3_out, and_4_out, and_5_out, and_6_out, and_7_out, and_8_out, and_9_out,
       and_10_out, and_11_out, and_12_out, and_13_out, and_14_out, and_15_out, and_16_out, and_17_out,
       and_18_out, and_19_out, and_20_out, and_21_out, and_22_out, and_23_out, and_24_out, and_25_out,
       and_26_out, and_27_out, and_28_out, and_29_out, and_30_out, and_31_out, and_32_out, and_33_out,
       and_34_out, and_35_out, and_36_out, and_37_out, and_38_out, and_39_out, and_40_out, and_41_out,
       and_42_out, and_43_out, and_44_out, and_45_out, and_46_out, and_47_out, and_48_out, and_49_out,
       not_1_out, not_2_out, not_3_out, not_4_out, not_5_out, not_6_out, not_7_out, not_8_out, not_9_out,
       not_10_out, not_11_out, not_12_out, not_13_out, not_14_out, not_15_out, not_16_out, not_17_out,
       not_18_out, not_19_out, not_20_out, not_21_out, not_22_out, not_23_out, not_24_out, not_25_out,
       not_26_out, not_27_out, not_28_out, not_29_out, not_30_out, not_31_out, not_32_out, not_33_out,
       not_34_out, not_35_out, not_36_out, not_37_out, not_38_out, not_39_out, not_40_out, not_41_out,
       not_42_out, not_43_out, not_44_out, not_45_out, not_46_out, not_47_out, not_48_out, not_49_out,
       not_50_out, not_51_out, not_52_out, not_53_out, not_54_out, not_55_out, not_56_out, not_57_out,
       not_58_out, not_59_out, not_60_out, not_61_out, not_62_out, not_63_out, not_64_out, not_65_out,
       not_66_out, not_67_out, not_68_out, not_69_out, not_70_out, not_71_out, not_72_out, not_73_out,
       not_74_out, not_75_out, not_76_out, not_77_out, not_78_out, not_79_out, not_80_out, not_81_out,
       not_82_out, not_83_out, not_84_out, not_85_out, not_86_out, not_87_out, not_88_out, not_89_out,
       not_90_out, not_91_out, not_92_out, not_93_out, not_94_out, not_95_out, not_96_out, not_97_out,
       not_98_out, not_99_out, not_100_out, not_101_out, not_102_out, not_103_out, not_104_out, not_105_out,
       not_106_out, not_107_out, not_108_out, not_109_out, not_110_out, not_111_out, not_112_out,
       not_113_out, not_114_out, not_115_out, not_116_out, not_117_out, not_118_out, not_119_out,
       not_120_out, not_121_out, not_122_out, not_123_out, not_124_out, not_125_out, not_126_out,
       not_127_out, not_128_out, not_129_out, not_130_out, not_131_out, not_132_out, not_133_out,
       not_134_out, not_135_out, not_136_out, not_137_out, not_138_out, not_139_out, not_140_out,
       not_141_out, not_142_out, not_143_out, not_144_out, not_145_out, not_146_out, not_147_out, or_8_out;

  not not_1 (not_1_out, E3);
  not not_2 (not_2_out, E4);
  not not_3 (not_3_out, E5);
  not not_4 (not_4_out, E1);
  not not_5 (not_5_out, E3);
  not not_6 (not_6_out, E4);
  not not_7 (not_7_out, E2);
  not not_8 (not_8_out, E3);
  not not_9 (not_9_out, E4);
  not not_10 (not_10_out, E1);
  not not_11 (not_11_out, E2);
  not not_12 (not_12_out, E3);
  not not_13 (not_13_out, E2);
  not not_14 (not_14_out, E3);
  not not_15 (not_15_out, E5);
  not not_16 (not_16_out, E1);
  not not_17 (not_17_out, E2);
  not not_18 (not_18_out, E5);
  not not_19 (not_19_out, E1);
  not not_20 (not_20_out, E4);
  not not_21 (not_21_out, E5);
  not not_22 (not_22_out, E2);
  not not_23 (not_23_out, E4);
  not not_24 (not_24_out, E5);
  not not_25 (not_25_out, E3);
  not not_26 (not_26_out, E4);
  not not_27 (not_27_out, E5);
  not not_28 (not_28_out, E1);
  not not_29 (not_29_out, E3);
  not not_30 (not_30_out, E4);
  not not_31 (not_31_out, E1);
  not not_32 (not_32_out, E2);
  not not_33 (not_33_out, E3);
  not not_34 (not_34_out, E1);
  not not_35 (not_35_out, E3);
  not not_36 (not_36_out, E5);
  not not_37 (not_37_out, E2);
  not not_38 (not_38_out, E3);
  not not_39 (not_39_out, E5);
  not not_40 (not_40_out, E1);
  not not_41 (not_41_out, E2);
  not not_42 (not_42_out, E5);
  not not_43 (not_43_out, E1);
  not not_44 (not_44_out, E2);
  not not_45 (not_45_out, E4);
  not not_46 (not_46_out, E2);
  not not_47 (not_47_out, E4);
  not not_48 (not_48_out, E5);
  not not_49 (not_49_out, E3);
  not not_50 (not_50_out, E4);
  not not_51 (not_51_out, E5);
  not not_52 (not_52_out, E1);
  not not_53 (not_53_out, E3);
  not not_54 (not_54_out, E4);
  not not_55 (not_55_out, E2);
  not not_56 (not_56_out, E3);
  not not_57 (not_57_out, E4);
  not not_58 (not_58_out, E1);
  not not_59 (not_59_out, E2);
  not not_60 (not_60_out, E3);
  not not_61 (not_61_out, E1);
  not not_62 (not_62_out, E3);
  not not_63 (not_63_out, E5);
  not not_64 (not_64_out, E2);
  not not_65 (not_65_out, E3);
  not not_66 (not_66_out, E5);
  not not_67 (not_67_out, E1);
  not not_68 (not_68_out, E2);
  not not_69 (not_69_out, E4);
  not not_70 (not_70_out, E1);
  not not_71 (not_71_out, E4);
  not not_72 (not_72_out, E5);
  not not_73 (not_73_out, E2);
  not not_74 (not_74_out, E4);
  not not_75 (not_75_out, E5);
  not not_76 (not_76_out, E3);
  not not_77 (not_77_out, E4);
  not not_78 (not_78_out, E5);
  not not_79 (not_79_out, E1);
  not not_80 (not_80_out, E3);
  not not_81 (not_81_out, E4);
  not not_82 (not_82_out, E2);
  not not_83 (not_83_out, E3);
  not not_84 (not_84_out, E4);
  not not_85 (not_85_out, E1);
  not not_86 (not_86_out, E2);
  not not_87 (not_87_out, E3);
  not not_88 (not_88_out, E1);
  not not_89 (not_89_out, E2);
  not not_90 (not_90_out, E5);
  not not_91 (not_91_out, E1);
  not not_92 (not_92_out, E4);
  not not_93 (not_93_out, E5);
  not not_94 (not_94_out, E2);
  not not_95 (not_95_out, E4);
  not not_96 (not_96_out, E5);
  not not_97 (not_97_out, E2);
  not not_98 (not_98_out, E3);
  not not_99 (not_99_out, E4);
  not not_100 (not_100_out, E1);
  not not_101 (not_101_out, E2);
  not not_102 (not_102_out, E3);
  not not_103 (not_103_out, E1);
  not not_104 (not_104_out, E2);
  not not_105 (not_105_out, E5);
  not not_106 (not_106_out, E2);
  not not_107 (not_107_out, E4);
  not not_108 (not_108_out, E5);
  not not_109 (not_109_out, E3);
  not not_110 (not_110_out, E4);
  not not_111 (not_111_out, E5);
  not not_112 (not_112_out, E2);
  not not_113 (not_113_out, E3);
  not not_114 (not_114_out, E4);
  not not_115 (not_115_out, E1);
  not not_116 (not_116_out, E2);
  not not_117 (not_117_out, E3);
  not not_118 (not_118_out, E1);
  not not_119 (not_119_out, E3);
  not not_120 (not_120_out, E5);
  not not_121 (not_121_out, E1);
  not not_122 (not_122_out, E4);
  not not_123 (not_123_out, E5);
  not not_124 (not_124_out, E2);
  not not_125 (not_125_out, E4);
  not not_126 (not_126_out, E5);
  not not_127 (not_127_out, E3);
  not not_128 (not_128_out, E4);
  not not_129 (not_129_out, E5);
  not not_130 (not_130_out, E1);
  not not_131 (not_131_out, E3);
  not not_132 (not_132_out, E4);
  not not_133 (not_133_out, E2);
  not not_134 (not_134_out, E3);
  not not_135 (not_135_out, E4);
  not not_136 (not_136_out, E1);
  not not_137 (not_137_out, E3);
  not not_138 (not_138_out, E5);
  not not_139 (not_139_out, E1);
  not not_140 (not_140_out, E2);
  not not_141 (not_141_out, E5);
  not not_142 (not_142_out, E1);
  not not_143 (not_143_out, E4);
  not not_144 (not_144_out, E5);
  not not_145 (not_145_out, E2);
  not not_146 (not_146_out, E4);
  not not_147 (not_147_out, E5);
  and and_1 (and_1_out, E1, E2, not_1_out, not_2_out, not_3_out);
  and and_2 (and_2_out, not_4_out, E2, not_5_out, not_6_out, E5);
  and and_3 (and_3_out, E1, not_7_out, not_8_out, not_9_out, E5);
  and and_4 (and_4_out, not_10_out, not_11_out, not_12_out, E4, E5);
  and and_5 (and_5_out, E1, not_13_out, not_14_out, E4, not_15_out);
  and and_6 (and_6_out, not_16_out, not_17_out, E3, E4, not_18_out);
  and and_7 (and_7_out, not_19_out, E2, E3, not_20_out, not_21_out);
  and and_8 (and_8_out, E1, not_22_out, E3, not_23_out, not_24_out);
  and and_9 (and_9_out, E1, E2, not_25_out, not_26_out, not_27_out);
  and and_10 (and_10_out, not_28_out, E2, not_29_out, not_30_out, E5);
  and and_11 (and_11_out, not_31_out, not_32_out, not_33_out, E4, E5);
  and and_12 (and_12_out, not_34_out, E2, not_35_out, E4, not_36_out);
  and and_13 (and_13_out, E1, not_37_out, not_38_out, E4, not_39_out);
  and and_14 (and_14_out, not_40_out, not_41_out, E3, E4, not_42_out);
  and and_15 (and_15_out, not_43_out, not_44_out, E3, not_45_out, E5);
  and and_16 (and_16_out, E1, not_46_out, E3, not_47_out, not_48_out);
  and and_17 (and_17_out, E1, E2, not_49_out, not_50_out, not_51_out);
  and and_18 (and_18_out, not_52_out, E2, not_53_out, not_54_out, E5);
  and and_19 (and_19_out, E1, not_55_out, not_56_out, not_57_out, E5);
  and and_20 (and_20_out, not_58_out, not_59_out, not_60_out, E4, E5);
  and and_21 (and_21_out, not_61_out, E2, not_62_out, E4, not_63_out);
  and and_22 (and_22_out, E1, not_64_out, not_65_out, E4, not_66_out);
  and and_23 (and_23_out, not_67_out, not_68_out, E3, not_69_out, E5);
  and and_24 (and_24_out, not_70_out, E2, E3, not_71_out, not_72_out);
  and and_25 (and_25_out, E1, not_73_out, E3, not_74_out, not_75_out);
  and and_26 (and_26_out, E1, E2, not_76_out, not_77_out, not_78_out);
  and and_27 (and_27_out, not_79_out, E2, not_80_out, not_81_out, E5);
  and and_28 (and_28_out, E1, not_82_out, not_83_out, not_84_out, E5);
  and and_29 (and_29_out, not_85_out, not_86_out, not_87_out, E4);
  and and_30 (and_30_out, not_88_out, not_89_out, E4, not_90_out);
  and and_31 (and_31_out, not_91_out, E2, E3, not_92_out, not_93_out);
  and and_32 (and_32_out, E1, not_94_out, E3, not_95_out, not_96_out);
  and and_33 (and_33_out, E1, not_97_out, not_98_out, not_99_out, E5);
  and and_34 (and_34_out, not_100_out, not_101_out, not_102_out, E4, E5);
  and and_35 (and_35_out, not_103_out, not_104_out, E3, E4, not_105_out);
  and and_36 (and_36_out, E1, not_106_out, E3, not_107_out, not_108_out);
  and and_37 (and_37_out, E1, E2, not_109_out, not_110_out, not_111_out);
  and and_38 (and_38_out, E1, not_112_out, not_113_out, not_114_out, E5);
  and and_39 (and_39_out, not_115_out, not_116_out, not_117_out, E4, E5);
  and and_40 (and_40_out, not_118_out, E2, not_119_out, E4, not_120_out);
  and and_41 (and_41_out, not_121_out, E2, E3, not_122_out, not_123_out);
  and and_42 (and_42_out, E1, not_124_out, E3, not_125_out, not_126_out);
  and and_43 (and_43_out, E1, E2, not_127_out, not_128_out, not_129_out);
  and and_44 (and_44_out, not_130_out, E2, not_131_out, not_132_out, E5);
  and and_45 (and_45_out, E1, not_133_out, not_134_out, not_135_out, E5);
  and and_46 (and_46_out, not_136_out, E2, not_137_out, E4, not_138_out);
  and and_47 (and_47_out, not_139_out, not_140_out, E3, E4, not_141_out);
  and and_48 (and_48_out, not_142_out, E2, E3, not_143_out, not_144_out);
  and and_49 (and_49_out, E1, not_145_out, E3, not_146_out, not_147_out);
  or or_1 (A9, and_1_out, and_2_out, and_3_out, and_4_out, and_5_out, and_6_out, and_7_out, and_8_out);
  or or_2 (B, and_9_out, and_10_out, and_11_out, and_12_out, and_13_out, and_14_out, and_15_out, and_16_out);
  or or_3 (C, and_17_out, and_18_out, and_19_out, and_20_out, and_21_out, and_22_out, and_23_out, and_24_out, and_25_out);
  or or_4 (D, and_26_out, and_27_out, and_28_out, and_29_out, and_30_out, and_31_out, and_32_out);
  or or_5 (E, and_33_out, and_34_out, and_35_out, and_36_out);
  or or_6 (F, and_37_out, and_38_out, and_39_out, and_40_out, and_41_out, and_42_out);
  or or_7 (G, and_43_out, and_44_out, and_45_out, and_46_out, and_47_out, and_48_out, and_49_out);
  _7_Segment_Display u_7_segment_display_1 (.g(G), .f(F), .a(A9), .b(B), .e(E), .d(D), .c(C));  // open: dp
  not not_148 (A, or_8_out);
  not not_149 (D_2, or_8_out);
  not not_150 (E_2, or_8_out);
  not not_151 (F_2, or_8_out);
  not not_152 (G_2, or_8_out);
  or or_8 (or_8_out, A9, B, C, D, E, F, G);
  _7_Segment_Display u_7_segment_display_2 (.g(G_2), .f(F_2), .a(A), .e(E_2), .d(D_2));  // open: b, c, dp

  // Notes on the sheet:
  //   SEGMENTO B
  //   SEGMENTO C
  //   SEGMENTO D
  //   SEGMENTO E
  //   SEGMENTO F
  //   SEGMENTO G
  //   SEGMENTO A
  //   A4
  //   A5
  //   B1
  //   B2
  //   B3
  //   B4
  //   B5
  //   B8
  //   A1
  //   A2
  //   A3
  //   A6
  //   A7
  //   A8
  //   B6
  //   B7
  //   C1
  //   C2
  //   C3
  //   C4
  //   C5
  //   C6
  //   C7
  //   C8
  //   C9
  //   D1
  //   D2
  //   D3
  //   D4
  //   D5
  //   D6
  //   D7
  //   Ee1
  //   Ee2
  //   Ee3
  //   Ee4
  //   F1
  //   F2
  //   F3
  //   F4
  //   F5
  //   F6
  //   G1
  //   G2
  //   G3
  //   G4
  //   G5
  //   G6
  //   G7
  //   B9
  //   C10
  //   SB
  //   SD
  //   D8
  //   SE
  //   Ee5
  //   F7
  //   G8
  //   SF
  //   GS
  //   SA
  //   or OrH(Erro, A9, B9, C10, D8, Ee5, F7, G8)
  //   A1
  //   D1
  //   E1
  //   F1
  //   G1
  //   Erro
endmodule
